// Logisim project PASSWORD_LOCK.circ as structural Verilog: 12 circuits, main circuit main
module main (
);

  wire ATTEMPT_out, CLEAR_KEYBOARD_out, clock_1_out, controlled_buffer_1_out, ENABLE_out, keyboard_1_avail,
       sub_circuit_2_1_clock, sub_circuit_2_1_enable, sub_circuit_2_1_password_attempt_failed,
       sub_circuit_2_1_password_set, sub_circuit_2_1_password_verified;
  wire [3:0] sub_circuit_2_1_chances_left_to_verify, sub_circuit_2_1_timer;
  wire [6:0] keyboard_1_data;
  wire [27:0] sub_circuit_2_1_l_28bit;

  Clock clock_1 (.out(clock_1_out));
  Button ENABLE (.out(ENABLE_out));
  Button ATTEMPT (.out(ATTEMPT_out));
  Hex_Digit_Display hex_digit_display_1 (.value(sub_circuit_2_1_chances_left_to_verify));  // open: dp
  Hex_Digit_Display hex_digit_display_2 (.value(sub_circuit_2_1_timer));  // open: dp
  assign controlled_buffer_1_out = keyboard_1_avail ? clock_1_out : 1'bz;  // Controlled_Buffer controlled_buffer_1
  Keyboard #(.buflen(4)) keyboard_1 (
    .clk(controlled_buffer_1_out), .clr(CLEAR_KEYBOARD_out), .avail(keyboard_1_avail), .data(keyboard_1_data));  // open: re
  Button CLEAR_KEYBOARD (.out(CLEAR_KEYBOARD_out));
  sub_circuit_2 sub_circuit_2_1 (
    .KEYBOARD(keyboard_1_data), .in_2(clock_1_out), .in_3(ENABLE_out), .ATTEMPT(ATTEMPT_out),
    .chances_left_to_verify(sub_circuit_2_1_chances_left_to_verify), .timer(sub_circuit_2_1_timer),
    .password_set(sub_circuit_2_1_password_set), .password_verified(sub_circuit_2_1_password_verified),
    .password_attempt_failed(sub_circuit_2_1_password_attempt_failed), .L_28bit(sub_circuit_2_1_l_28bit),
    .clock(sub_circuit_2_1_clock), .enable(sub_circuit_2_1_enable));
  LED PASSWORD_HAS_BEEN_SET (.in(sub_circuit_2_1_password_set));
  LED PASSWORD_HAS_BEEN_VERIFIED (.in(sub_circuit_2_1_password_verified));
  LED PASSWORD_ATTEMPT_MADE (.in(sub_circuit_2_1_password_attempt_failed));
  TTY #(.cols(1), .rows(1)) tty_1 (
    .data(sub_circuit_2_1_l_28bit[6:0]), .clk(sub_circuit_2_1_clock), .clr(sub_circuit_2_1_enable));  // open: we
  TTY #(.cols(1), .rows(1)) tty_2 (
    .data(sub_circuit_2_1_l_28bit[13:7]), .clk(sub_circuit_2_1_clock), .clr(sub_circuit_2_1_enable));  // open: we
  TTY #(.cols(1), .rows(1)) tty_3 (
    .data(sub_circuit_2_1_l_28bit[20:14]), .clk(sub_circuit_2_1_clock), .clr(sub_circuit_2_1_enable));  // open: we
  TTY #(.cols(1), .rows(1)) tty_4 (
    .data(sub_circuit_2_1_l_28bit[27:21]), .clk(sub_circuit_2_1_clock), .clr(sub_circuit_2_1_enable));  // open: we

  // Notes on the sheet:
  //   ATTEMPTS 
  //   LEFT TO
  //   VERIFY
  //   PASSWORD
  //   PLEASE
  //   FOR
  //   WAIT
  //   SECONDS
  //   TO
  //   RESTART
  //   PLEASE ENTER HERE
  //   VERIFIED
  //   PASSWORD
  //   DISPLAY
endmodule

module register (
  input  [6:0] Keyboard,
  input  Clear_password,
  input  Enable,
  input  Clock,
  output [27:0] Output,
  output [2:0] Not_needed
);

  wire and_1_out, AND_2_out, input_counter_1_clock, OR_out;
  wire [6:0] log_register_q0, log_register_q1, log_register_q2;

  Shift_Register #(.length(4), .width(7)) log_register (
    .in(Keyboard), .clk(and_1_out), .clr(Clear_password), .q0(log_register_q0), .q1(log_register_q1),
    .q2(log_register_q2));  // open: shift, out, load, d0, d1, d2, d3, q3
  or OR (OR_out, Keyboard[6], Keyboard[5], Keyboard[4], Keyboard[3], Keyboard[2], Keyboard[1], Keyboard[0]);
  Register #(.width(7)) register_1 (
    .D(log_register_q2), .en(Enable), .Q(Output[6:0]), .clk(and_1_out), .clr(Clear_password));
  Register #(.width(7)) register_2 (
    .D(log_register_q1), .en(Enable), .Q(Output[13:7]), .clk(and_1_out), .clr(Clear_password));
  Register #(.width(7)) register_3 (
    .D(log_register_q0), .en(Enable), .Q(Output[20:14]), .clk(and_1_out), .clr(Clear_password));
  Register #(.width(7)) register_4 (
    .D(Keyboard), .en(Enable), .Q(Output[27:21]), .clk(and_1_out), .clr(Clear_password));
  and and_1 (and_1_out, input_counter_1_clock, OR_out, Clock);
  DotMatrix #(.inputtype("row"), .matrixcols(7), .matrixrows(1)) dotmatrix_1 (.row0(Output[6:0]));
  DotMatrix #(.inputtype("row"), .matrixcols(7), .matrixrows(1)) dotmatrix_2 (.row0(Output[13:7]));
  DotMatrix #(.inputtype("row"), .matrixcols(7), .matrixrows(1)) dotmatrix_3 (.row0(Output[20:14]));
  DotMatrix #(.inputtype("row"), .matrixcols(7), .matrixrows(1)) dotmatrix_4 (.row0(Output[27:21]));
  and AND_2 (AND_2_out, Clock, OR_out);
  Input_counter input_counter_1 (
    .in_3(AND_2_out), .Input_5(3'b101), .Clear(Clear_password), .\output (Not_needed),
    .Clock(input_counter_1_clock));  // open: Load_not_needed, Data_in_not_needed

  // Notes on the sheet:
  //   data 1
  //   data 2
  //   data 3
  //   data 4
  //   INPUT
  //   COUNTER
endmodule

module Input_counter (
  input  Load_not_needed,
  input  [2:0] Data_in_not_needed,
  input  in_3,
  input  [2:0] Input_5,
  input  Clear,
  output [2:0] \output ,
  output Clock
);

  wire and_1_out, comparator_1_eq;

  and and_1 (and_1_out, in_3, Clock);
  Counter #(.max('h7), .width(3)) counter_1 (
    .load(Load_not_needed), .D(Data_in_not_needed), .count(1'b1), .Q(\output ), .clk(and_1_out), .clr(Clear));  // open: carry, up
  Comparator #(.width(3)) comparator_1 (.a(\output ), .b(Input_5), .eq(comparator_1_eq));  // open: gt, lt
  not not_1 (Clock, comparator_1_eq);
endmodule

module comparator (
  input  [27:0] Input_1,
  input  [27:0] Input_2,
  output Output
);

  Comparator #(.width(28)) comparator_1 (.a(Input_1), .b(Input_2), .eq(Output));  // open: gt, lt
endmodule

module L_28_bit_adder (
  input  [27:0] \input ,
  output \output 
);

  wire or_1_out;

  or or_1 (or_1_out, \input [0], \input [1], \input [2], \input [3], \input [4], \input [5], \input [6], \input [7], \input [8], \input [9], \input [10], \input [11], \input [12], \input [13], \input [14], \input [15], \input [16], \input [17], \input [18], \input [19], \input [20], \input [21], \input [22], \input [23], \input [24], \input [25], \input [26]);
  or or_2 (\output , or_1_out, \input [27]);
endmodule

module sub_circuit_1 (
  input  Enable1,
  input  CLEAR_PASSWORD,
  input  [6:0] KEYBOARD,
  input  CLOCK,
  input  Enable2,
  input  CLEAR_INPUT,
  output [27:0] view_password_not_needed,
  output PASSWORD_SET,
  output PASSWORD_VERIFIED,
  output PASSWORD_ATTEMPT,
  output [27:0] view_attempt_not_needed
);

  register register_1 (
    .Keyboard(KEYBOARD), .Clear_password(CLEAR_PASSWORD), .Enable(Enable1), .Clock(CLOCK),
    .Output(view_password_not_needed));  // open: Not_needed
  register register_2 (
    .Keyboard(KEYBOARD), .Clear_password(CLEAR_INPUT), .Enable(Enable2), .Clock(CLOCK),
    .Output(view_attempt_not_needed));  // open: Not_needed
  L_28_bit_adder l_28_bit_adder_1 (.\input (view_password_not_needed), .\output (PASSWORD_SET));
  comparator comparator_1 (
    .Input_1(view_password_not_needed), .Input_2(view_attempt_not_needed), .Output(PASSWORD_VERIFIED));
  L_28_bit_adder l_28_bit_adder_2 (.\input (view_attempt_not_needed), .\output (PASSWORD_ATTEMPT));

  // Notes on the sheet:
  //   REGISTER
  //   REGISTER
  //   28 BIT ADDER
  //   COMPARATOR
  //   28 BIT ADDER
endmodule

module sub_circuit_2 (
  input  [6:0] KEYBOARD,
  input  in_2,
  input  in_3,
  input  ATTEMPT,
  output password_set,
  output password_verified,
  output password_attempt_failed,
  output [27:0] L_28bit,
  output clock,
  output enable,
  output [3:0] chances_left_to_verify,
  output [3:0] timer
);

  wire AND_out, comparator_1_eq, enable_1_output, l9_to_0_counter_1_out_5, not_1_out, or_1_out, OR_2_out,
       rectify_1_enable_input, sub_circuit_1_1_password_verified, XNOR_out;
  wire [2:0] input_counter_1_output;

  rectify rectify_1 (.ENABLE(in_3), .chances_input(chances_left_to_verify), .enable_input(rectify_1_enable_input));
  enable enable_1 (.enable(rectify_1_enable_input), .ATTEMPT(ATTEMPT), .OUTPUT(enable_1_output));
  Chances_counter chances_counter_1 (.Input({1'b0, input_counter_1_output}), .Output(chances_left_to_verify));
  xnor XNOR (XNOR_out, comparator_1_eq, enable_1_output);
  sub_circuit_1 sub_circuit_1_1 (
    .Enable1(enable_1_output), .CLEAR_PASSWORD(rectify_1_enable_input), .KEYBOARD(KEYBOARD), .CLOCK(in_2),
    .Enable2(XNOR_out), .CLEAR_INPUT(or_1_out), .PASSWORD_SET(password_set),
    .PASSWORD_VERIFIED(sub_circuit_1_1_password_verified), .PASSWORD_ATTEMPT(password_attempt_failed),
    .view_attempt_not_needed(L_28bit));  // open: view_password_not_needed
  or or_1 (or_1_out, rectify_1_enable_input, ATTEMPT);
  not not_1 (not_1_out, sub_circuit_1_1_password_verified);
  and AND (AND_out, not_1_out, ATTEMPT);
  or OR_2 (OR_2_out, sub_circuit_1_1_password_verified, l9_to_0_counter_1_out_5);
  Input_counter input_counter_1 (
    .in_3(AND_out), .Input_5(3'b100), .Clear(OR_2_out), .\output (input_counter_1_output));  // open: Load_not_needed, Data_in_not_needed, Clock
  and and_2 (clock, password_set, sub_circuit_1_1_password_verified);
  Comparator #(.width(3)) comparator_1 (.a(input_counter_1_output), .b(3'b100), .eq(comparator_1_eq));  // open: gt, lt
  or or_3 (enable, rectify_1_enable_input, ATTEMPT);
  L9_to_0_counter l9_to_0_counter_1 (
    .Clock(in_2), .Start(comparator_1_eq), .Reset(l9_to_0_counter_1_out_5), .Output(timer),
    .out_5(l9_to_0_counter_1_out_5));

  assign password_verified = clock;

  // Notes on the sheet:
  //   ENABLE
  //   CHANCES
  //   COUNTER
  //   SUB
  //   CIRCUIT 1
  //   INPUT
  //   COUNTER
  //   CMP
  //   9 T0 0
  //   COUNTER
endmodule

module L9_to_0_counter (
  input  Clock,
  input  Start,
  input  Reset,
  output [3:0] Output,
  output out_5
);

  wire and_1_out, comparator_1_gt, comparator_1_lt, or_1_out;
  wire [3:0] counter_1_q;

  Counter #(.max('hf), .width(4)) counter_1 (
    .count(1'b1), .Q(counter_1_q), .clk(and_1_out), .clr(Reset));  // open: load, D, carry, up
  and and_1 (and_1_out, Clock, Start, or_1_out);
  Subtractor #(.width(4)) subtractor_1 (.a(4'b1001), .b(counter_1_q), .out(Output));  // open: bin, bout
  Comparator #(.width(4)) comparator_1 (
    .a(4'b1001), .b(counter_1_q), .gt(comparator_1_gt), .lt(comparator_1_lt));  // open: eq
  or or_1 (or_1_out, comparator_1_gt, comparator_1_lt);
  not not_1 (out_5, or_1_out);
endmodule

module Chances_counter (
  input  [3:0] Input,
  output [3:0] Output
);

  Subtractor #(.width(4)) subtractor_1 (.a(4'b0011), .b(Input), .out(Output));  // open: bin, bout
endmodule

module enable (
  input  enable,
  input  ATTEMPT,
  output OUTPUT
);

  D_Flip_Flop d_ff_1 (.D(1'b1), .clk(enable), .Q(OUTPUT), .reset(ATTEMPT));  // open: Qn, preset
endmodule

module rectify (
  input  ENABLE,
  input  [3:0] chances_input,
  output enable_input
);

  wire comparator_1_eq;
  wire [3:0] and_1_out;
  wire [3:3] not_1_out;

  not not_1 (not_1_out[3], comparator_1_eq);
  Comparator #(.width(4)) comparator_1 (.a(chances_input), .b(4'b1111), .eq(comparator_1_eq));  // open: gt, lt
  assign and_1_out = {4{ENABLE}} & {4{not_1_out[3]}};  // AND_Gate and_1, 4 bits wide
  or or_1 (enable_input, and_1_out[0], and_1_out[1], and_1_out[2], and_1_out[3]);
endmodule

module reset (
  input  reset,
  input  set_change_password,
  input  in_3,
  input  ATTEMPT,
  input  [3:0] chances_input,
  output set_password,
  output remove_password
);

  wire d_ff_1_q, rectify_1_enable_input;

  rectify rectify_1 (.ENABLE(reset), .chances_input(chances_input), .enable_input(rectify_1_enable_input));
  D_Flip_Flop d_ff_1 (.clk(rectify_1_enable_input), .Q(d_ff_1_q), .reset(ATTEMPT));  // open: D, Qn, preset
  D_Flip_Flop d_ff_2 (.D(set_change_password), .clk(d_ff_1_q), .Q(set_password), .reset(ATTEMPT));  // open: Qn, preset
  D_Flip_Flop d_ff_3 (.D(in_3), .clk(d_ff_1_q), .Q(remove_password), .reset(ATTEMPT));  // open: Qn, preset
endmodule
